// Logisim project MIPS_Light.circ as structural Verilog: 18 circuits, main circuit main
module main (
);

  wire clock_1_out, controle_1_en_mon, controle_1_en_ram, controle_1_en_tec, controle_1_rd_ram,
       controle_1_sel_op2, controle_1_sel_ula, controle_1_wr_acc, controle_1_wr_ram;
  wire [1:0] controle_1_sel_op1;
  wire [5:0] dados_1_opcode;
  wire [6:0] ascii_1_s1, ascii_2_s2, keyboard_1_data;
  wire [23:0] dados_1_add_imed;
  wire [31:0] controle_1_dout_rom, dados_1_din_bus, ram_1_data;

  TTY tty_1 (.data(ascii_1_s1), .clk(clock_1_out), .we(controle_1_en_mon));  // open: clr
  ASCII ascii_1 (.A(dados_1_din_bus), .S1(ascii_1_s1));  // open: B, S2
  Keyboard keyboard_1 (.clk(clock_1_out), .re(controle_1_en_tec), .data(keyboard_1_data));  // open: clr, avail
  RAM #(.addrWidth(24), .dataWidth(32), .bus("separate")) ram_1 (
    .addr(dados_1_add_imed), .din(dados_1_din_bus), .data(ram_1_data), .str(controle_1_wr_ram),
    .sel(controle_1_en_ram), .clk(clock_1_out), .ld(controle_1_rd_ram));  // open: clr
  ASCII ascii_2 (.B(keyboard_1_data), .S2(ascii_2_s2));  // open: A, S1
  dados dados_1 (
    .dout_ROM(controle_1_dout_rom), .ADD_IMED(dados_1_add_imed), .DOUT_BUS(ram_1_data),
    .SEL_OP1(controle_1_sel_op1), .DOUT_TEC(ascii_2_s2), .SEL_OP2(controle_1_sel_op2),
    .WR_ACC(controle_1_wr_acc), .DIN_BUS(dados_1_din_bus), .SEL_ULA(controle_1_sel_ula), .clk(clock_1_out),
    .opcode(dados_1_opcode));
  Clock clock_1 (.out(clock_1_out));
  controle controle_1 (
    .opcode(dados_1_opcode), .EN_RAM(controle_1_en_ram), .WR_RAM(controle_1_wr_ram),
    .RD_RAM(controle_1_rd_ram), .WR_ACC(controle_1_wr_acc), .SEL_OP1(controle_1_sel_op1),
    .SEL_OP2(controle_1_sel_op2), .SEL_ULA(controle_1_sel_ula), .EN_TEC(controle_1_en_tec),
    .EN_MON(controle_1_en_mon), .ADD_IMED(dados_1_add_imed), .clk(clock_1_out), .DOUT_ROM(controle_1_dout_rom));
endmodule

module dados (
  input  [31:0] dout_ROM,
  input  [31:0] DOUT_BUS,
  input  [1:0] SEL_OP1,
  input  [6:0] DOUT_TEC,
  input  SEL_OP2,
  input  WR_ACC,
  input  SEL_ULA,
  input  clk,
  output [5:0] opcode,
  output [23:0] ADD_IMED,
  output [31:0] DIN_BUS
);

  wire [25:24] register_1_q;
  wire [31:0] bit_extender_1_out, bit_extender_2_out, multiplexer_1_out, multiplexer_2_out, ula_1_s;

  assign bit_extender_1_out = {{25{1'b0}}, DOUT_TEC};  // Bit_Extender bit_extender_1
  Multiplexer #(.width(32), .enable("false")) multiplexer_1 (
    .in0(DOUT_BUS), .in1(bit_extender_2_out), .out(multiplexer_1_out), .sel(SEL_OP2));
  Register #(.width(32)) register_1 (
    .D(dout_ROM), .en(1'b1), .Q({opcode, register_1_q, ADD_IMED}), .clk(clk), .clr(1'b0));
  assign bit_extender_2_out = {{8{1'b0}}, ADD_IMED};  // Bit_Extender bit_extender_2
  ULA ula_1 (.A(DIN_BUS), .B(multiplexer_1_out), .sel_ULA(SEL_ULA), .S(ula_1_s));
  Multiplexer #(.select(2), .width(32), .enable("false")) multiplexer_2 (
    .in0(DOUT_BUS), .in1(bit_extender_2_out), .in2(ula_1_s), .in3(bit_extender_1_out),
    .out(multiplexer_2_out), .sel(SEL_OP1));
  Register #(.width(32)) ACC (.D(multiplexer_2_out), .en(WR_ACC), .Q(DIN_BUS), .clk(clk), .clr(1'b0));
endmodule

module ULA (
  input  [31:0] A,
  input  [31:0] B,
  input  sel_ULA,
  output [31:0] S
);

  wire [31:0] adder_1_out, subtractor_1_out;

  Adder #(.width(32)) adder_1 (.a(A), .b(B), .out(adder_1_out));  // open: cin, cout
  Subtractor #(.width(32)) subtractor_1 (.a(A), .b(B), .out(subtractor_1_out));  // open: bin, bout
  Multiplexer #(.width(32), .enable("false")) multiplexer_1 (
    .in0(adder_1_out), .in1(subtractor_1_out), .out(S), .sel(sel_ULA));
endmodule

module controle (
  input  [23:0] ADD_IMED,
  input  [5:0] opcode,
  input  clk,
  output [31:0] DOUT_ROM,
  output EN_RAM,
  output WR_RAM,
  output RD_RAM,
  output WR_ACC,
  output [1:0] SEL_OP1,
  output SEL_OP2,
  output SEL_ULA,
  output EN_TEC,
  output EN_MON
);

  wire control_logic_1_en_pc, control_logic_1_reset_pc, control_logic_1_sel_jump;
  wire [23:0] pc_1_in_rom;

  Control_Logic control_logic_1 (
    .OPCODE(opcode), .EN_RAM(EN_RAM), .WR_RAM(WR_RAM), .RD_RAM(RD_RAM), .WR_ACC(WR_ACC), .SEL_OP1(SEL_OP1),
    .SEL_OP2(SEL_OP2), .SEL_ULA(SEL_ULA), .EN_TEC(EN_TEC), .EN_MON(EN_MON),
    .SEL_JUMP(control_logic_1_sel_jump), .EN_PC(control_logic_1_en_pc), .RESET_PC(control_logic_1_reset_pc));
  PC pc_1 (
    .ADD_IMED(ADD_IMED), .EN_PC(control_logic_1_en_pc), .SEL_JUMP(control_logic_1_sel_jump), .clk(clk),
    .RESET(control_logic_1_reset_pc), .in_ROM(pc_1_in_rom));
  ROM #(.addrWidth(24), .dataWidth(32)) rom_1 (.addr(pc_1_in_rom), .data(DOUT_ROM));  // open: sel

  // Notes on the sheet:
  //   contents of rom_1 (hex, n*v repeats v):
  //   24000000 28000000 14000001 20000001
endmodule

module PC (
  input  [23:0] ADD_IMED,
  input  EN_PC,
  input  SEL_JUMP,
  input  RESET,
  input  clk,
  output [23:0] in_ROM
);

  wire and_1_out, not_1_out;
  wire [23:0] counter_1_q;

  not not_1 (not_1_out, SEL_JUMP);
  and and_1 (and_1_out, EN_PC, not_1_out);
  Counter #(.width(24), .max('hffffff), .trigger("falling")) counter_1 (
    .load(SEL_JUMP), .D(ADD_IMED), .count(and_1_out), .Q(counter_1_q), .clk(clk), .clr(RESET));  // open: carry
  Multiplexer #(.width(24), .enable("false")) multiplexer_1 (
    .in0(counter_1_q), .in1(ADD_IMED), .out(in_ROM), .sel(SEL_JUMP));
endmodule

module Control_Logic (
  input  [5:0] OPCODE,
  output EN_RAM,
  output WR_RAM,
  output RD_RAM,
  output WR_ACC,
  output [1:0] SEL_OP1,
  output SEL_OP2,
  output SEL_ULA,
  output EN_TEC,
  output EN_MON,
  output SEL_JUMP,
  output EN_PC,
  output RESET_PC
);

  EN_RAM u_EN_RAM (.A(OPCODE), .EN_RAM(EN_RAM));
  WR_RAM u_WR_RAM (.A(OPCODE), .WR_RAM(WR_RAM));
  RD_RAM u_RD_RAM (.A(OPCODE), .RD_RAM(RD_RAM));
  WR_ACC u_WR_ACC (.A(OPCODE), .WR_ACC(WR_ACC));
  SEL_OP1 u_SEL_OP1 (.A(OPCODE), .SEL_OP1(SEL_OP1));
  SEL_OP2 u_SEL_OP2 (.A(OPCODE), .SEL_OP2(SEL_OP2));
  SEL_ULA u_SEL_ULA (.A(OPCODE), .SEL_ULA(SEL_ULA));
  EN_TEC u_EN_TEC (.A(OPCODE), .EN_TEC(EN_TEC));
  EN_MON u_EN_MON (.A(OPCODE), .EN_MON(EN_MON));
  SEL_JUMP u_SEL_JUMP (.A(OPCODE), .SEL_JUMP(SEL_JUMP));
  EN_PC en_pc_1 (.A(OPCODE), .EN_PC(EN_PC), .RESET_PC(RESET_PC));
endmodule

module EN_RAM (
  input  [5:0] A,
  output EN_RAM
);

  wire and_1_out, and_2_out, and_3_out, not_1_out, not_2_out, not_3_out, not_4_out, not_5_out, not_6_out,
       not_7_out;

  not not_1 (not_1_out, A[2]);
  not not_2 (not_2_out, A[3]);
  not not_3 (not_3_out, A[0]);
  not not_4 (not_4_out, A[3]);
  not not_5 (not_5_out, A[0]);
  not not_6 (not_6_out, A[3]);
  not not_7 (not_7_out, A[1]);
  and and_1 (and_1_out, not_2_out, A[1], not_3_out);
  and and_2 (and_2_out, not_4_out, A[2], not_5_out);
  and and_3 (and_3_out, not_6_out, not_1_out, not_7_out, A[0]);
  or or_1 (EN_RAM, and_1_out, and_2_out, and_3_out);
endmodule

module WR_RAM (
  input  [5:0] A,
  output WR_RAM
);

  wire not_1_out, not_2_out, not_3_out;

  not not_1 (not_1_out, A[3]);
  not not_2 (not_2_out, A[2]);
  not not_3 (not_3_out, A[1]);
  and and_1 (WR_RAM, not_1_out, not_2_out, not_3_out, A[0]);
endmodule

module RD_RAM (
  input  [5:0] A,
  output RD_RAM
);

  wire and_1_out, and_2_out, not_1_out, not_2_out, not_3_out, not_4_out;

  not not_1 (not_1_out, A[3]);
  not not_2 (not_2_out, A[0]);
  not not_3 (not_3_out, A[3]);
  not not_4 (not_4_out, A[0]);
  and and_1 (and_1_out, not_1_out, A[1], not_2_out);
  and and_2 (and_2_out, not_3_out, A[2], not_4_out);
  or or_1 (RD_RAM, and_1_out, and_2_out);
endmodule

module WR_ACC (
  input  [5:0] A,
  output WR_ACC
);

  wire and_1_out, and_2_out, and_3_out, not_1_out, not_2_out, not_3_out, not_4_out;

  not not_1 (not_1_out, A[3]);
  not not_2 (not_2_out, A[3]);
  not not_3 (not_3_out, A[2]);
  not not_4 (not_4_out, A[1]);
  and and_1 (and_1_out, not_1_out, A[1]);
  and and_2 (and_2_out, not_2_out, A[2]);
  and and_3 (and_3_out, A[3], not_3_out, not_4_out, A[0]);
  or or_1 (WR_ACC, and_1_out, and_2_out, and_3_out);
endmodule

module SEL_OP1 (
  input  [5:0] A,
  output [1:0] SEL_OP1
);

  wire and_1_out, and_2_out, and_3_out, not_1_out, not_2_out, not_3_out, not_4_out, not_5_out, not_6_out,
       not_7_out;

  not not_1 (not_1_out, A[3]);
  not not_2 (not_2_out, A[2]);
  not not_3 (not_3_out, A[0]);
  not not_4 (not_4_out, A[2]);
  not not_5 (not_5_out, A[1]);
  not not_6 (not_6_out, A[3]);
  not not_7 (not_7_out, A[2]);
  and and_1 (and_1_out, not_1_out, not_2_out, A[1], not_3_out);
  and and_2 (and_2_out, A[3], not_4_out, not_5_out, A[0]);
  and and_3 (and_3_out, not_6_out, not_7_out, A[1], A[0]);
  or or_1 (SEL_OP1[1], and_1_out, and_2_out);
  or or_2 (SEL_OP1[0], and_2_out, and_3_out);
endmodule

module SEL_OP2 (
  input  [5:0] A,
  output SEL_OP2
);

  wire not_1_out, not_2_out;

  not not_1 (not_1_out, A[3]);
  not not_2 (not_2_out, A[0]);
  and and_1 (SEL_OP2, not_1_out, A[2], not_2_out);
endmodule

module SEL_ULA (
  input  [5:0] A,
  output SEL_ULA
);

  wire not_1_out;

  not not_1 (not_1_out, A[3]);
  and and_1 (SEL_ULA, not_1_out, A[2], A[1]);
endmodule

module EN_TEC (
  input  [5:0] A,
  output EN_TEC
);

  wire not_1_out, not_2_out;

  not not_1 (not_1_out, A[2]);
  not not_2 (not_2_out, A[1]);
  and and_1 (EN_TEC, A[3], not_1_out, not_2_out, A[0]);
endmodule

module EN_MON (
  input  [5:0] A,
  output EN_MON
);

  wire not_1_out, not_2_out;

  not not_1 (not_1_out, A[2]);
  not not_2 (not_2_out, A[0]);
  and and_1 (EN_MON, A[3], not_1_out, A[1], not_2_out);
endmodule

module SEL_JUMP (
  input  [5:0] A,
  output SEL_JUMP
);

  wire not_1_out, not_2_out, not_3_out;

  not not_1 (not_1_out, A[2]);
  not not_2 (not_2_out, A[1]);
  not not_3 (not_3_out, A[0]);
  and and_1 (SEL_JUMP, A[3], not_1_out, not_2_out, not_3_out);
endmodule

module EN_PC (
  input  [5:0] A,
  output EN_PC,
  output RESET_PC
);

  wire not_1_out, not_2_out, not_3_out, not_4_out;

  not not_1 (not_1_out, A[1]);
  not not_2 (not_2_out, A[2]);
  or or_1 (EN_PC, A[0], A[1], A[2], A[3]);
  not not_3 (not_3_out, A[0]);
  not not_4 (not_4_out, A[3]);
  and and_1 (RESET_PC, not_3_out, not_1_out, not_2_out, not_4_out);
endmodule

module ASCII (
  input  [31:0] A,
  input  [6:0] B,
  output [6:0] S1,
  output [6:0] S2
);

  wire [31:0] adder_1_out;

  Adder #(.width(32)) adder_1 (.a(A), .b(32'h30), .out(adder_1_out));  // open: cin, cout
  Subtractor #(.width(7)) subtractor_1 (.a(B), .b(7'b0110000), .out(S2));  // open: bin, bout
  Bit_Extender #(.in_width(32), .out_width(7)) bit_extender_1 (.in(adder_1_out), .out(S1));
endmodule
